// Logisim project Controller.circ as structural Verilog: 9 circuits, main circuit main
module main (
  input  reset,
  input  [4:0] leftYin,
  input  [4:0] rightYin,
  input  clock,
  output [4:0] zero,
  output [4:0] ballX,
  output [4:0] ballY,
  output [4:0] leftYout,
  output [4:0] rightYout,
  output [7:0] scoreB,
  output [7:0] vxy,
  output lose,
  output win,
  output [7:0] scoreA,
  output [7:0] xball,
  output [7:0] yball
);

  wire adder_2_cout, adder_3_cout, adder_7_cout, adder_8_cout, and_2_out, and_4_out, Bcontact,
       comparator_2_eq, comparator_2_gt, comparator_3_eq, comparator_3_gt, en1, \end , hitA, hitB,
       inrange_1_sharearrow, inrange_2_sharearrow, not_1_out, not_2_out, not_3_out, not_4_out, not_5_out,
       or_1_out, or_2_out, or_4_out, or_6_out, RBcontact, vxzero, xor_1_out, xor_2_out, xor_3_out, xor_4_out;
  wire [2:0] change_vy_1_vy_2, controlled_buffer_1_out, multiplexer_4_out, multiplexer_6_out, reflect_1_newv,
       reflect_2_newv;
  wire [4:0] from_8_to_5_bits_1_out, from_8_to_5_bits_2_out, from_8_to_5_bits_3_out, multiplexer_2_out,
       multiplexer_5_out;
  wire [7:0] adder_1_out, adder_4_out, adder_5_out, adder_6_out, extend_2_out, inc8_1_r, inc8_2_r,
       multiplexer_1_out, multiplexer_3_out, vx_ext;

  extend extend_1 (.in(vxy[2:0]), .out(vx_ext));
  extend extend_2 (.in(vxy[5:3]), .out(extend_2_out));
  Adder adder_1 (.a(xball), .b(vx_ext), .out(adder_1_out));  // open: cin, cout
  Multiplexer #(.width(8), .enable("false")) multiplexer_1 (
    .in0(adder_1_out), .in1(8'hc0), .out(multiplexer_1_out), .sel(reset));
  Adder adder_2 (.a(vx_ext), .b(xball), .cout(adder_2_cout));  // open: out, cin
  Adder adder_3 (.a(extend_2_out), .b(yball), .cout(adder_3_cout));  // open: out, cin
  Register #(.trigger("falling")) xreg (.D(multiplexer_1_out), .en(en1), .Q(xball), .clk(clock), .clr(\end ));
  not not_1 (not_1_out, vx_ext[7]);
  xor xor_1 (xor_1_out, vx_ext[7], adder_2_cout);
  xor xor_2 (xor_2_out, extend_2_out[7], adder_3_cout);
  or or_1 (or_1_out, reset, vxzero);
  Multiplexer #(.width(5), .enable("false")) multiplexer_2 (
    .in0(rightYin), .in1(5'b01111), .out(multiplexer_2_out), .sel(or_1_out));
  Adder adder_4 (.a(xball), .b(8'h1c), .out(adder_4_out));  // open: cin, cout
  and and_1 (hitA, vx_ext[7], xor_1_out);
  not not_2 (not_2_out, xor_1_out);
  and and_2 (and_2_out, not_2_out, not_3_out);
  not not_3 (not_3_out, Bcontact);
  Adder adder_5 (.a(yball), .b(extend_2_out), .out(adder_5_out));  // open: cin, cout
  Register #(.width(5), .trigger("falling")) rightYreg (
    .D(multiplexer_2_out), .en(not_4_out), .Q(rightYout), .clk(clock), .clr(\end ));
  not not_4 (not_4_out, vx_ext[7]);
  Adder adder_6 (.a(xball), .b(8'he4), .out(adder_6_out));  // open: cin, cout
  and and_3 (hitB, not_1_out, xor_1_out);
  Multiplexer #(.width(8), .enable("false")) multiplexer_3 (
    .in0(adder_5_out), .in1(8'h80), .out(multiplexer_3_out), .sel(reset));
  or or_2 (or_2_out, not_5_out, reset);
  not not_5 (not_5_out, xor_2_out);
  Adder adder_7 (.a(adder_6_out), .b(vx_ext), .cout(adder_7_cout));  // open: out, cin
  Adder adder_8 (.a(vx_ext), .b(adder_4_out), .cout(adder_8_cout));  // open: out, cin
  or or_3 (en1, and_2_out, reset);
  Register #(.trigger("falling")) yreg (.D(multiplexer_3_out), .en(or_2_out), .Q(yball), .clk(clock), .clr(\end ));
  Comparator #(.width(3)) comparator_1 (.a(vxy[2:0]), .b(3'b000), .eq(vxzero));  // open: gt, lt
  xor xor_3 (xor_3_out, adder_7_cout, vx_ext[7]);
  xor xor_4 (xor_4_out, adder_8_cout, vx_ext[7]);
  from_8_to_5_bits from_8_to_5_bits_1 (.in(yball), .out(from_8_to_5_bits_1_out));
  from_8_to_5_bits from_8_to_5_bits_2 (.in(yball), .out(from_8_to_5_bits_2_out));
  or or_4 (or_4_out, reset, Bcontact, xor_1_out);
  reflect reflect_1 (.oldv(vxy[2:0]), .newv(reflect_1_newv));
  Multiplexer #(.width(3), .enable("false")) multiplexer_4 (
    .in0(reflect_1_newv), .in1(3'b110), .out(multiplexer_4_out), .sel(reset));
  Multiplexer #(.width(5), .enable("false")) multiplexer_5 (
    .in0(leftYin), .in1(rightYout), .out(multiplexer_5_out), .sel(RBcontact));
  from_8_to_5_bits from_8_to_5_bits_3 (.in(yball), .out(from_8_to_5_bits_3_out));
  inrange inrange_1 (.Yball(from_8_to_5_bits_1_out), .Ybat(leftYin), .shareArrow(inrange_1_sharearrow));
  inrange inrange_2 (.Yball(from_8_to_5_bits_2_out), .Ybat(rightYout), .shareArrow(inrange_2_sharearrow));
  Register #(.width(3)) vx (.D(multiplexer_4_out), .en(or_4_out), .Q(vxy[2:0]), .clk(clock), .clr(\end ));
  and and_4 (and_4_out, inrange_1_sharearrow, xor_3_out);
  and and_5 (RBcontact, inrange_2_sharearrow, xor_4_out);
  reflect reflect_2 (.oldv(vxy[5:3]), .newv(reflect_2_newv));
  change_vy change_vy_1 (
    .batY(multiplexer_5_out), .ballY(from_8_to_5_bits_3_out), .vy(vxy[5:3]), .vy_2(change_vy_1_vy_2));
  assign controlled_buffer_1_out = Bcontact ? change_vy_1_vy_2 : 3'bz;  // Controlled_Buffer controlled_buffer_1
  inc8 inc8_1 (.X(scoreB), .R(inc8_1_r));
  inc8 inc8_2 (.X(scoreA), .R(inc8_2_r));
  or or_5 (Bcontact, and_4_out, RBcontact);
  // Probe on controlled_buffer_1_out
  Pull_Resistor pull_resistor_1 (.node(controlled_buffer_1_out));
  assign controlled_buffer_1_out = xor_2_out ? reflect_2_newv : 3'bz;  // Controlled_Buffer controlled_buffer_2
  Register scB (.D(inc8_1_r), .en(hitB), .Q(scoreB), .clk(clock), .clr(\end ));
  Register scA (.D(inc8_2_r), .en(hitA), .Q(scoreA), .clk(clock), .clr(\end ));
  Multiplexer #(.width(3), .enable("false")) multiplexer_6 (
    .in0(controlled_buffer_1_out), .in1(3'b001), .out(multiplexer_6_out), .sel(reset));
  or or_6 (or_6_out, Bcontact, xor_2_out, reset);
  // Probe on vxy[5:3]
  Register #(.width(3)) vy (.D(multiplexer_6_out), .en(or_6_out), .Q(vxy[5:3]), .clk(clock), .clr(\end ));
  Comparator #(.mode("unsigned")) comparator_2 (
    .a(scoreB), .b(8'hb), .gt(comparator_2_gt), .eq(comparator_2_eq));  // open: lt
  Comparator #(.mode("unsigned")) comparator_3 (
    .a(scoreA), .b(8'hb), .gt(comparator_3_gt), .eq(comparator_3_eq));  // open: lt
  or or_7 (win, comparator_2_gt, comparator_2_eq);
  or or_8 (lose, comparator_3_gt, comparator_3_eq);
  or or_9 (\end , lose, win);
  from_8_to_5_bits from_8_to_5_bits_4 (.in(xball), .out(ballX));
  from_8_to_5_bits from_8_to_5_bits_5 (.in(yball), .out(ballY));

  assign leftYout = leftYin;
  assign vxy[7:6] = 2'b00;
  assign zero = {5{1'b0}};

  // Other names for the same wires on the sheet: LeftBat[4:0] = leftYin; RightBat[4:0] = rightYout; vxneg = vx_ext[7];
  //   vx[2:0] = vxy[2:0]; vy[2:0] = vxy[5:3]; xreg[7:0] = xball; yreg[7:0] = yball

  // Notes on the sheet:
  //   Note:
  //   longVX
  //   longVY
  //   Outputs for CdM8
  //   vxneg
  //   yxneg
  //   xrefl
  //   yrefl
  //   hitA
  //   Note:
  //   hitB
  //   Note:
  //   These guys are waiting for the contact between
  //    the ball and the "gates" to change the score.
  //   This register stores coordinates of right bat
  //   Note:
  //   Note:
  //   LBcontact
  //   RBcontact
  //   These signlas let us know whether the ball touches one of the bats.
  //   Bcontact
  //   This is register. Each register keeps one of the variables that we use in calculations.
  //   Note:
  //   Note:
  //   This part is keeping the score and checking who is the winner.
  //   Outputs for controller
endmodule

module reflect (
  input  [2:0] oldv,
  output [2:0] newv
);

  wire comparator_1_eq;
  wire [2:0] inc3_1_r, not_1_out;

  Comparator #(.width(3)) comparator_1 (.a(3'b100), .b(oldv), .eq(comparator_1_eq));  // open: gt, lt
  assign not_1_out = ~oldv;  // NOT_Gate not_1, 3 bits wide
  inc3 inc3_1 (.X(not_1_out), .R(inc3_1_r));
  Multiplexer #(.width(3), .enable("false")) multiplexer_1 (
    .in0(inc3_1_r), .in1(not_1_out), .out(newv), .sel(comparator_1_eq));

  // Notes on the sheet:
  //   Note:
  //   This chip is used to change the ball speed after reflecting from bats or walls.
endmodule

module inc3 (
  input  [2:0] X,
  output [2:0] R
);

  wire [2:1] and_1_out;
  wire [2:2] and_1_out_2;

  assign {and_1_out_2[2], and_1_out} = {and_1_out, 1'b1} & X;  // AND_Gate and_1, 3 bits wide
  assign R = X ^ {and_1_out, 1'b1};  // XOR_Gate xor_1, 3 bits wide
  // Probe on and_1_out_2[2]
endmodule

module inrange (
  input  [4:0] Yball,
  input  [4:0] Ybat,
  output shareArrow
);

  wire comparator_1_eq, comparator_2_eq, comparator_3_eq;
  wire [4:0] adder_1_out, adder_2_out;

  Adder #(.width(5)) adder_1 (.a(Ybat), .b(5'b00001), .out(adder_1_out));  // open: cin, cout
  Adder #(.width(5)) adder_2 (.a(Ybat), .b(5'b00010), .out(adder_2_out));  // open: cin, cout
  Comparator #(.width(5)) comparator_1 (.a(Yball), .b(Ybat), .eq(comparator_1_eq));  // open: gt, lt
  Comparator #(.width(5)) comparator_2 (.a(Yball), .b(adder_1_out), .eq(comparator_2_eq));  // open: gt, lt
  Comparator #(.width(5)) comparator_3 (.a(Yball), .b(adder_2_out), .eq(comparator_3_eq));  // open: gt, lt
  or or_1 (shareArrow, comparator_1_eq, comparator_2_eq, comparator_3_eq);

  // Notes on the sheet:
  //   Note:
  //   This chip is checking wether the ball touches the bat or not.
endmodule

module extend (
  input  [2:0] in,
  output [7:0] out
);

  wire comparator_1_eq, comparator_1_gt, or_1_out;

  // Probe on in
  Comparator #(.width(3)) comparator_1 (.a(in), .b(3'b000), .gt(comparator_1_gt), .eq(comparator_1_eq));  // open: lt
  or or_1 (or_1_out, comparator_1_gt, comparator_1_eq);
  Multiplexer #(.enable("false")) multiplexer_1 (.in0(1'b1), .in1(1'b0), .out(out[7]), .sel(or_1_out));
  // Probe on {{5{out[7]}}, in}

  assign out[6:0] = {{4{out[7]}}, in};

  // Notes on the sheet:
  //   Note:
  //   Note:
  //   This chip extends 5-bit number to 8-bit
endmodule

module from_8_to_5_bits (
  input  [7:0] in,
  output [4:0] out
);


  assign out = in[7:3];
endmodule

module inc8 (
  input  [7:0] X,
  output [7:0] R
);

  wire [7:0] and_1_out;

  assign and_1_out = {and_1_out[6:0], 1'b1} & X;  // AND_Gate and_1, 8 bits wide
  assign R = X ^ {and_1_out[6:0], 1'b1};  // XOR_Gate xor_1, 8 bits wide
  // Probe on and_1_out[7]
endmodule

module change_vy (
  input  [4:0] batY,
  input  [4:0] ballY,
  input  [2:0] vy,
  output [2:0] vy_2
);

  wire and_1_out, and_2_out, and_3_out, comparator_1_eq, comparator_2_eq, comparator_3_eq, comparator_4_eq,
       comparator_5_eq, comparator_6_eq, comparator_7_eq, or_1_out, or_2_out;
  wire [2:0] controlled_buffer_1_out, dec3_1_r, inc3_1_r, vy_t;
  wire [4:0] adder_1_out, adder_2_out;

  Adder #(.width(5)) adder_1 (.a(batY), .b(5'b00010), .out(adder_1_out));  // open: cin, cout
  Adder #(.width(5)) adder_2 (.a(batY), .b(5'b00001), .out(adder_2_out));  // open: cin, cout
  Comparator #(.width(5), .mode("unsigned")) comparator_1 (
    .a(adder_1_out), .b(ballY), .eq(comparator_1_eq));  // open: gt, lt
  Comparator #(.width(3)) comparator_2 (.a(vy_t), .b(3'b100), .eq(comparator_2_eq));  // open: gt, lt
  Comparator #(.width(5), .mode("unsigned")) comparator_3 (
    .a(adder_2_out), .b(ballY), .eq(comparator_3_eq));  // open: gt, lt
  Comparator #(.width(3), .mode("unsigned")) comparator_4 (.a(vy_t), .b(3'b011), .eq(comparator_4_eq));  // open: gt, lt
  Comparator #(.width(5), .mode("unsigned")) comparator_5 (.a(ballY), .b(batY), .eq(comparator_5_eq));  // open: gt, lt
  // Probe on vy_t
  reflect reflect_1 (.oldv(vy), .newv(vy_t));
  or or_1 (or_1_out, comparator_1_eq, comparator_2_eq);
  Comparator #(.width(3)) comparator_6 (.a(vy_t), .b(3'b111), .eq(comparator_6_eq));  // open: gt, lt
  Comparator #(.width(3)) comparator_7 (.a(vy_t), .b(3'b001), .eq(comparator_7_eq));  // open: gt, lt
  or or_2 (or_2_out, comparator_4_eq, comparator_5_eq);
  inc3 inc3_1 (.X(vy_t), .R(inc3_1_r));
  dec3 dec3_1 (.X(vy_t), .R(dec3_1_r));
  and and_1 (and_1_out, or_1_out, ~comparator_6_eq, ~comparator_3_eq, ~comparator_4_eq);  // AND_Gate
  and and_2 (and_2_out, ~comparator_7_eq, ~comparator_3_eq, ~comparator_2_eq, or_2_out);  // AND_Gate
  and and_3 (and_3_out, ~and_2_out, ~and_1_out);  // AND_Gate
  assign controlled_buffer_1_out = and_1_out ? inc3_1_r : 3'bz;  // Controlled_Buffer controlled_buffer_1
  assign controlled_buffer_1_out = and_3_out ? vy_t : 3'bz;  // Controlled_Buffer controlled_buffer_2
  assign controlled_buffer_1_out = and_2_out ? dec3_1_r : 3'bz;  // Controlled_Buffer controlled_buffer_3
  Pull_Resistor pull_resistor_1 (.node(controlled_buffer_1_out));
  // Probe on controlled_buffer_1_out
  // Probe on vy_2
  reflect reflect_2 (.oldv(controlled_buffer_1_out), .newv(vy_2));

  // Notes on the sheet:
  //   Note:
  //   This chip changes ball's speed in rage from -4 to 3, when the ball hits one of the bats.
endmodule

module dec3 (
  input  [2:0] X,
  output [2:0] R
);

  wire [2:0] or_1_out;

  assign or_1_out = {or_1_out[1:0], 1'b0} | X;  // OR_Gate or_1, 3 bits wide
  // Probe on or_1_out[2]
  assign R = ~(X ^ {or_1_out[1:0], 1'b0});  // XNOR_Gate xnor_1, 3 bits wide
endmodule
