// Logisim project Main.circ as structural Verilog: 6 circuits, main circuit chip
module main (
  input  [4:0] bus_0
);

  wire clock_1_out, R_out;
  wire [3:0] n10_1_one, n10_1_ten, n10_2_one, n10_2_ten;
  wire [4:0] joystick_1_y, main_1_ballx, main_1_bally, main_1_leftyout, main_1_rightyout, main_1_zero,
       not_1_out, videosystem_1_ballx_2, videosystem_1_bally_2, videosystem_1_chipid_2,
       videosystem_1_leftbaty_2, videosystem_1_rightbaty_2, videosystem_2_ballx_2, videosystem_2_bally_2,
       videosystem_2_chipid_2, videosystem_2_leftbaty_2, videosystem_2_rightbaty_2, videosystem_3_ballx_2,
       videosystem_3_bally_2, videosystem_3_chipid_2, videosystem_3_leftbaty_2, videosystem_3_rightbaty_2;
  wire [7:0] Ls, Rs;
  wire [31:0] videosystem_1_output, videosystem_1_output_2, videosystem_1_output_3, videosystem_1_output_4,
       videosystem_1_output_5, videosystem_1_output_6, videosystem_1_output_7, videosystem_1_output_8,
       videosystem_2_output, videosystem_2_output_2, videosystem_2_output_3, videosystem_2_output_4,
       videosystem_2_output_5, videosystem_2_output_6, videosystem_2_output_7, videosystem_2_output_8,
       videosystem_3_output, videosystem_3_output_2, videosystem_3_output_3, videosystem_3_output_4,
       videosystem_3_output_5, videosystem_3_output_6, videosystem_3_output_7, videosystem_3_output_8,
       videosystem_4_output, videosystem_4_output_2, videosystem_4_output_3, videosystem_4_output_4,
       videosystem_4_output_5, videosystem_4_output_6, videosystem_4_output_7, videosystem_4_output_8;

  Hex_Digit_Display hex_digit_display_1 (.value(n10_1_one));  // open: dp
  Hex_Digit_Display hex_digit_display_2 (.value(n10_1_ten));  // open: dp
  _10 u_10_1 (.ten(n10_1_ten), .one(n10_1_one), .\input (Rs));
  Joystick #(.bits(5)) joystick_1 (.y(joystick_1_y));  // open: x
  Button R (.out(R_out));
  assign not_1_out = ~joystick_1_y;  // NOT_Gate not_1, 5 bits wide
  Controller_main main_1 (
    .rightYin(bus_0), .zero(main_1_zero), .ballX(main_1_ballx), .ballY(main_1_bally),
    .rightYout(main_1_rightyout), .leftYout(main_1_leftyout), .reset(R_out), .leftYin(not_1_out),
    .scoreA(Rs), .scoreB(Ls), .clock(clock_1_out));  // open: xball, yball, vxy, win, lose
  Clock clock_1 (.out(clock_1_out));
  DotMatrix #(.matrixcols(32), .matrixrows(32)) dotmatrix_1 (
    .col0(videosystem_1_output), .col1(videosystem_1_output_2), .col2(videosystem_1_output_3),
    .col3(videosystem_1_output_4), .col4(videosystem_1_output_5), .col5(videosystem_1_output_6),
    .col6(videosystem_1_output_7), .col7(videosystem_1_output_8), .col8(videosystem_2_output),
    .col9(videosystem_2_output_2), .col10(videosystem_2_output_3), .col11(videosystem_2_output_4),
    .col12(videosystem_2_output_5), .col13(videosystem_2_output_6), .col14(videosystem_2_output_7),
    .col15(videosystem_2_output_8), .col16(videosystem_3_output), .col17(videosystem_3_output_2),
    .col18(videosystem_3_output_3), .col19(videosystem_3_output_4), .col20(videosystem_3_output_5),
    .col21(videosystem_3_output_6), .col22(videosystem_3_output_7), .col23(videosystem_3_output_8),
    .col24(videosystem_4_output), .col25(videosystem_4_output_2), .col26(videosystem_4_output_3),
    .col27(videosystem_4_output_4), .col28(videosystem_4_output_5), .col29(videosystem_4_output_6),
    .col30(videosystem_4_output_7), .col31(videosystem_4_output_8));
  videosystem videosystem_1 (
    .chipID(main_1_zero), .ballX(main_1_ballx), .ballY(main_1_bally), .leftbatY(main_1_leftyout),
    .rightbatY(main_1_rightyout), .chipID_2(videosystem_1_chipid_2), .ballX_2(videosystem_1_ballx_2),
    .ballY_2(videosystem_1_bally_2), .leftbatY_2(videosystem_1_leftbaty_2),
    .rightbatY_2(videosystem_1_rightbaty_2), .\output (videosystem_1_output),
    .output_2(videosystem_1_output_2), .output_3(videosystem_1_output_3), .output_4(videosystem_1_output_4),
    .output_5(videosystem_1_output_5), .output_6(videosystem_1_output_6), .output_7(videosystem_1_output_7),
    .output_8(videosystem_1_output_8));
  videosystem videosystem_2 (
    .chipID(videosystem_1_chipid_2), .ballX(videosystem_1_ballx_2), .ballY(videosystem_1_bally_2),
    .leftbatY(videosystem_1_leftbaty_2), .rightbatY(videosystem_1_rightbaty_2),
    .chipID_2(videosystem_2_chipid_2), .ballX_2(videosystem_2_ballx_2), .ballY_2(videosystem_2_bally_2),
    .leftbatY_2(videosystem_2_leftbaty_2), .rightbatY_2(videosystem_2_rightbaty_2),
    .\output (videosystem_2_output), .output_2(videosystem_2_output_2), .output_3(videosystem_2_output_3),
    .output_4(videosystem_2_output_4), .output_5(videosystem_2_output_5), .output_6(videosystem_2_output_6),
    .output_7(videosystem_2_output_7), .output_8(videosystem_2_output_8));
  videosystem videosystem_3 (
    .chipID(videosystem_2_chipid_2), .ballX(videosystem_2_ballx_2), .ballY(videosystem_2_bally_2),
    .leftbatY(videosystem_2_leftbaty_2), .rightbatY(videosystem_2_rightbaty_2),
    .chipID_2(videosystem_3_chipid_2), .ballX_2(videosystem_3_ballx_2), .ballY_2(videosystem_3_bally_2),
    .leftbatY_2(videosystem_3_leftbaty_2), .rightbatY_2(videosystem_3_rightbaty_2),
    .\output (videosystem_3_output), .output_2(videosystem_3_output_2), .output_3(videosystem_3_output_3),
    .output_4(videosystem_3_output_4), .output_5(videosystem_3_output_5), .output_6(videosystem_3_output_6),
    .output_7(videosystem_3_output_7), .output_8(videosystem_3_output_8));
  videosystem videosystem_4 (
    .chipID(videosystem_3_chipid_2), .ballX(videosystem_3_ballx_2), .ballY(videosystem_3_bally_2),
    .leftbatY(videosystem_3_leftbaty_2), .rightbatY(videosystem_3_rightbaty_2),
    .\output (videosystem_4_output), .output_2(videosystem_4_output_2), .output_3(videosystem_4_output_3),
    .output_4(videosystem_4_output_4), .output_5(videosystem_4_output_5), .output_6(videosystem_4_output_6),
    .output_7(videosystem_4_output_7), .output_8(videosystem_4_output_8));  // open: chipID_2, ballX_2, ballY_2, leftbatY_2, rightbatY_2
  Hex_Digit_Display hex_digit_display_3 (.value(n10_2_ten));  // open: dp
  Hex_Digit_Display hex_digit_display_4 (.value(n10_2_one));  // open: dp
  _10 u_10_2 (.ten(n10_2_ten), .one(n10_2_one), .\input (Ls));
endmodule

module videosystem (
  input  [4:0] chipID,
  input  [4:0] ballX,
  input  [4:0] ballY,
  input  [4:0] leftbatY,
  input  [4:0] rightbatY,
  output [31:0] \output ,
  output [31:0] output_2,
  output [31:0] output_3,
  output [31:0] output_4,
  output [31:0] output_5,
  output [31:0] output_6,
  output [31:0] output_7,
  output [31:0] output_8,
  output [4:0] chipID_2,
  output [4:0] ballX_2,
  output [4:0] ballY_2,
  output [4:0] leftbatY_2,
  output [4:0] rightbatY_2
);

  wire [4:0] chip_1_ballx_2, chip_1_bally_2, chip_1_chipid_2, chip_1_leftbaty_2, chip_1_rightbaty_2,
       chip_2_ballx_2, chip_2_bally_2, chip_2_chipid_2, chip_2_leftbaty_2, chip_2_rightbaty_2,
       chip_3_ballx_2, chip_3_bally_2, chip_3_chipid_2, chip_3_leftbaty_2, chip_3_rightbaty_2,
       chip_4_ballx_2, chip_4_bally_2, chip_4_chipid_2, chip_4_leftbaty_2, chip_4_rightbaty_2,
       chip_5_ballx_2, chip_5_bally_2, chip_5_chipid_2, chip_5_leftbaty_2, chip_5_rightbaty_2,
       chip_6_ballx_2, chip_6_bally_2, chip_6_chipid_2, chip_6_leftbaty_2, chip_6_rightbaty_2,
       chip_7_ballx_2, chip_7_bally_2, chip_7_chipid_2, chip_7_leftbaty_2, chip_7_rightbaty_2;

  chip chip_1 (
    .chipID(chipID), .ballX(ballX), .ballY(ballY), .leftbatY(leftbatY), .rightbatY(rightbatY),
    .\output (\output ), .chipID_2(chip_1_chipid_2), .ballX_2(chip_1_ballx_2), .ballY_2(chip_1_bally_2),
    .leftbatY_2(chip_1_leftbaty_2), .rightbatY_2(chip_1_rightbaty_2));
  chip chip_2 (
    .chipID(chip_1_chipid_2), .ballX(chip_1_ballx_2), .ballY(chip_1_bally_2), .leftbatY(chip_1_leftbaty_2),
    .rightbatY(chip_1_rightbaty_2), .\output (output_2), .chipID_2(chip_2_chipid_2),
    .ballX_2(chip_2_ballx_2), .ballY_2(chip_2_bally_2), .leftbatY_2(chip_2_leftbaty_2),
    .rightbatY_2(chip_2_rightbaty_2));
  chip chip_3 (
    .chipID(chip_4_chipid_2), .ballX(chip_4_ballx_2), .ballY(chip_4_bally_2), .leftbatY(chip_4_leftbaty_2),
    .rightbatY(chip_4_rightbaty_2), .\output (output_4), .chipID_2(chip_3_chipid_2),
    .ballX_2(chip_3_ballx_2), .ballY_2(chip_3_bally_2), .leftbatY_2(chip_3_leftbaty_2),
    .rightbatY_2(chip_3_rightbaty_2));
  chip chip_4 (
    .chipID(chip_2_chipid_2), .ballX(chip_2_ballx_2), .ballY(chip_2_bally_2), .leftbatY(chip_2_leftbaty_2),
    .rightbatY(chip_2_rightbaty_2), .\output (output_3), .chipID_2(chip_4_chipid_2),
    .ballX_2(chip_4_ballx_2), .ballY_2(chip_4_bally_2), .leftbatY_2(chip_4_leftbaty_2),
    .rightbatY_2(chip_4_rightbaty_2));
  chip chip_5 (
    .chipID(chip_6_chipid_2), .ballX(chip_6_ballx_2), .ballY(chip_6_bally_2), .leftbatY(chip_6_leftbaty_2),
    .rightbatY(chip_6_rightbaty_2), .\output (output_7), .chipID_2(chip_5_chipid_2),
    .ballX_2(chip_5_ballx_2), .ballY_2(chip_5_bally_2), .leftbatY_2(chip_5_leftbaty_2),
    .rightbatY_2(chip_5_rightbaty_2));
  chip chip_6 (
    .chipID(chip_7_chipid_2), .ballX(chip_7_ballx_2), .ballY(chip_7_bally_2), .leftbatY(chip_7_leftbaty_2),
    .rightbatY(chip_7_rightbaty_2), .\output (output_6), .chipID_2(chip_6_chipid_2),
    .ballX_2(chip_6_ballx_2), .ballY_2(chip_6_bally_2), .leftbatY_2(chip_6_leftbaty_2),
    .rightbatY_2(chip_6_rightbaty_2));
  chip chip_7 (
    .chipID(chip_3_chipid_2), .ballX(chip_3_ballx_2), .ballY(chip_3_bally_2), .leftbatY(chip_3_leftbaty_2),
    .rightbatY(chip_3_rightbaty_2), .\output (output_5), .chipID_2(chip_7_chipid_2),
    .ballX_2(chip_7_ballx_2), .ballY_2(chip_7_bally_2), .leftbatY_2(chip_7_leftbaty_2),
    .rightbatY_2(chip_7_rightbaty_2));
  chip chip_8 (
    .chipID(chip_5_chipid_2), .ballX(chip_5_ballx_2), .ballY(chip_5_bally_2), .leftbatY(chip_5_leftbaty_2),
    .rightbatY(chip_5_rightbaty_2), .\output (output_8), .chipID_2(chipID_2), .ballX_2(ballX_2),
    .ballY_2(ballY_2), .leftbatY_2(leftbatY_2), .rightbatY_2(rightbatY_2));
endmodule

module chip (
  input  [4:0] chipID,
  input  [4:0] ballX,
  input  [4:0] ballY,
  input  [4:0] leftbatY,
  input  [4:0] rightbatY,
  output [31:0] \output ,
  output [4:0] chipID_2,
  output [4:0] ballX_2,
  output [4:0] ballY_2,
  output [4:0] leftbatY_2,
  output [4:0] rightbatY_2
);

  wire comparator_1_eq, comparator_2_eq, comparator_3_eq;
  wire [31:0] multiplexer_1_out, multiplexer_2_out, multiplexer_3_out, shifter_1_out, shifter_2_out,
       shifter_3_out;

  Multiplexer #(.width(32), .enable("false")) multiplexer_1 (
    .in0({32{1'b0}}), .in1(shifter_1_out), .out(multiplexer_1_out), .sel(comparator_1_eq));
  Comparator #(.width(5)) comparator_1 (.a(chipID), .b(ballX), .eq(comparator_1_eq));  // open: gt, lt
  Shifter #(.width(32)) shifter_1 (.in(32'h1), .\dist (ballY), .out(shifter_1_out));
  Comparator #(.width(5)) comparator_2 (.a(5'b00011), .b(chipID), .eq(comparator_2_eq));  // open: gt, lt
  Shifter #(.width(32)) shifter_2 (.in(32'h7), .\dist (leftbatY), .out(shifter_2_out));
  Comparator #(.width(5)) comparator_3 (.a(5'b11100), .b(chipID), .eq(comparator_3_eq));  // open: gt, lt
  Shifter #(.width(32)) shifter_3 (.in(32'h7), .\dist (rightbatY), .out(shifter_3_out));
  assign \output  = multiplexer_1_out | multiplexer_2_out | multiplexer_3_out;  // OR_Gate or_1, 32 bits wide
  Multiplexer #(.width(32), .enable("false")) multiplexer_2 (
    .in0({32{1'b0}}), .in1(shifter_2_out), .out(multiplexer_2_out), .sel(comparator_2_eq));
  Multiplexer #(.width(32), .enable("false")) multiplexer_3 (
    .in0({32{1'b0}}), .in1(shifter_3_out), .out(multiplexer_3_out), .sel(comparator_3_eq));
  inc inc_1 (.X(chipID), .R(chipID_2));

  assign ballX_2 = ballX;
  assign ballY_2 = ballY;
  assign leftbatY_2 = leftbatY;
  assign rightbatY_2 = rightbatY;
endmodule

module inc (
  input  [4:0] X,
  output [4:0] R
);

  wire [4:1] and_1_out;
  wire [4:4] and_1_out_2;

  assign {and_1_out_2[4], and_1_out} = {and_1_out, 1'b1} & X;  // AND_Gate and_1, 5 bits wide
  assign R = X ^ {and_1_out, 1'b1};  // XOR_Gate xor_1, 5 bits wide
  // Probe on and_1_out_2[4]
endmodule

module dec (
  input  [4:0] X,
  output [4:0] R
);

  wire [4:1] or_1_out;
  wire [4:4] or_1_out_2;

  assign {or_1_out_2[4], or_1_out} = {or_1_out, 1'b0} | X;  // OR_Gate or_1, 5 bits wide
  assign R = ~(X ^ {or_1_out, 1'b0});  // XNOR_Gate xnor_1, 5 bits wide
  // Probe on or_1_out_2[4]
endmodule

module _10 (
  input  [7:0] \input ,
  output [3:0] ten,
  output [3:0] one
);

  wire [7:3] divider_1_out;
  wire [7:4] divider_1_rem;

  // Probe on \input 
  // Probe on {1'b0, ten[2:0]}
  Divider divider_1 (
    .a({4'b0000, \input [3:0]}), .b(8'ha), .out({divider_1_out, ten[2:0]}), .upper({\input [7:4], 4'b0000}),
    .rem({divider_1_rem, one}));
  // Probe on one

  assign ten[3] = 1'b0;
endmodule
