// Logisim project ScorePrinter.circ as structural Verilog: 1 circuit, main circuit main
module main (
  input  [2:0] _3bit_input,
  output center,
  output topleft,
  output top,
  output topright,
  output bottomleft,
  output bottom,
  output bottomright
);

  ROM #(.addrWidth(3), .dataWidth(7)) rom_1 (
    .addr(_3bit_input), .data({bottomright, bottom, bottomleft, topright, top, topleft, center}));  // open: sel

  // Notes on the sheet:
  //   contents of rom_1 (hex, n*v repeats v):
  //   7e 48 3d 6d 4b 67 77 4c
endmodule
