// Logisim project Software.circ as structural Verilog: 1 circuit, main circuit main
module main (
  input  [7:0] xball,
  input  [7:0] yball,
  input  [7:0] vxy,
  input  bus_0,
  output [4:0] rightYin
);

  wire and_3_out, cdm_8_mark5_1_p1, cdm_8_mark5_1_p2, cdm_8_mark5_1_p4, cdm_8_mark5_1_p5, cdm_8_mark5_1_p6,
       cdm_8_mark5_1_p7, data, instr, IO_3_2_out, IO_3_out, IO_4_out, IO_5_out, not_1_out, not_2_out, port,
       rd_d, rd_wr, wr_d;
  wire [2:0] register_1_q;
  wire [7:0] addr, cdm_8_mark5_1_p10, cdm_8_mark5_1_p11, controlled_buffer_2_out;

  // Probe on cdm_8_mark5_1_p2
  // Probe on cdm_8_mark5_1_p1
  // Probe on cdm_8_mark5_1_p4
  // Probe on cdm_8_mark5_1_p5
  Decoder #(.disabled(0)) decoder_1 (.out0(instr), .out1(data), .sel(cdm_8_mark5_1_p6), .en(cdm_8_mark5_1_p7));
  // CdM_8_mark5 cdm_8_mark5_1: pin names not known; wires that end beside it: cdm_8_mark5_1_p1, cdm_8_mark5_1_p2, bus_0, cdm_8_mark5_1_p4, cdm_8_mark5_1_p5, cdm_8_mark5_1_p6, cdm_8_mark5_1_p7, rd_wr, addr, cdm_8_mark5_1_p10, cdm_8_mark5_1_p11, rd_wr
  not not_1 (not_1_out, rd_wr);
  assign cdm_8_mark5_1_p11 = rd_wr ? controlled_buffer_2_out : 8'bz;  // Controlled_Buffer controlled_buffer_1
  and and_1 (rd_d, rd_wr, cdm_8_mark5_1_p6);
  and and_2 (wr_d, ~rd_wr, cdm_8_mark5_1_p6);  // AND_Gate
  assign controlled_buffer_2_out = not_1_out ? cdm_8_mark5_1_p10 : 8'bz;  // Controlled_Buffer controlled_buffer_2
  and and_3 (and_3_out, port, data);
  ROM rom_1 (.addr(addr), .data(controlled_buffer_2_out), .sel(instr));
  RAM ram_1 (.addr(addr), .data(controlled_buffer_2_out), .sel(and_3_out), .clk(bus_0), .ld(rd_wr));  // open: clr
  nor nor_1 (port, IO_4_out, IO_5_out, IO_3_out);
  not not_2 (not_2_out, wr_d);
  and IO_4 (IO_4_out, rd_d, ~addr[0], ~addr[1], addr[2], ~addr[3]);  // AND_Gate
  assign controlled_buffer_2_out = IO_4_out ? xball : 8'bz;  // Controlled_Buffer controlled_buffer_3
  and IO_5 (IO_5_out, rd_d, addr[0], ~addr[1], addr[2], ~addr[3]);  // AND_Gate
  assign controlled_buffer_2_out = IO_5_out ? yball : 8'bz;  // Controlled_Buffer controlled_buffer_4
  and IO_3 (IO_3_out, rd_d, addr[0], addr[1], ~addr[2], ~addr[3]);  // AND_Gate
  assign controlled_buffer_2_out = IO_3_out ? vxy : 8'bz;  // Controlled_Buffer controlled_buffer_5
  and IO_3_2 (IO_3_2_out, not_2_out, addr[0], addr[1], ~addr[2], ~addr[3]);  // AND_Gate
  // Probe on {rightYin, register_1_q}
  Register register_1 (
    .D(controlled_buffer_2_out), .en(IO_3_2_out), .Q({rightYin, register_1_q}), .clk(bus_0));  // open: clr

  // Other names for the same wires on the sheet: clock = bus_0

  // Notes on the sheet:
  //   instr memory 
  //   data memory 
  //   contents of rom_1 (hex, n*v repeats v):
  //   d1 e0 d2 f4 ba 36 a 92 d3 0 d0 f3 b0 98 98 98 d1 4 71 e1 26 d1 f5 b5 96 e3 1c 8f 96 e3 20 8f 36 e2
  //   24 8f ee 9a d1 5 71 e1 3d d1 f5 b5 8 96 e3 33 8f 12 e3 37 8f 36 e2 3b 8f ee 9a d1 6 71 e1 4f d1 f5
  //   b5 96 e3 49 8f 36 e2 4d 8f ee 9a d1 7 71 e1 5d d1 f5 b5 36 e2 5b 8f ee 9a 0 e1 65 d2 f5 ba ee 9a d1
  //   1 71 e1 73 d1 f5 b5 16 e3 71 8f ee 9a d1 2 71 e1 85 d1 f5 b5 96 e3 7f 8f 16 e3 83 8f ee 9a d1 3 71
  //   e1 9a d1 f5 b5 8 96 e3 92 8f 12 e3 96 8f 16 e3 9a 8f 9b e3 9e 86 d0 f3 a2 ee
endmodule
